# Fritzing sketch sketch (saved by Fritzing 0.9.5d)
breadboards: 1

parts:
  Компонент1 = Arduino Uno (Rev3) - ICSP
  R1 = Resistor [tolerance=±5% resistance=220 package="0603 [SMD]"]
  R2 = Resistor [tolerance=±5% resistance=220 package="0603 [SMD]"]
  R3 = Resistor [tolerance=±5% resistance=220 package="0603 [SMD]"]
  R4 = Resistor [tolerance=±5% resistance=220 package="0603 [SMD]"]
  R5 = Resistor [tolerance=±5% resistance=220 package="0603 [SMD]"]
  R6 = Resistor [tolerance=±5% resistance=220 package="0603 [SMD]"]
  R7 = Resistor [tolerance=±5% resistance=220 package="0603 [SMD]"]
  R8 = Resistor [tolerance=±5% resistance=220 package="0603 [SMD]"]
  S1 = Pushbutton [package="[THT]"]
  J1 = Piezo Speaker

nets:
  N1: Компонент1.D8, R7.Pin_1
  N2: Компонент1.D9_PWM, R4.Pin_1
  N3: Компонент1.D10_PWM/SS, R5.Pin_1
  N4: Компонент1.D11_PWM/MOSI, J1.pin2
  N5: Компонент1.D13/SCK, S1.Pin_1, S1.Pin_2
  N6: Компонент1.GND, S1.Pin_3, S1.Pin_4, J1.pin1
  N7: Компонент1.D2, R1.Pin_0, R2.Pin_0, R3.Pin_0, R4.Pin_0, R5.Pin_0
  N8: Компонент1.D3_PWM, R1.Pin_1
  N9: Компонент1.D4, R2.Pin_1
  N10: Компонент1.D5_PWM, R3.Pin_1
  N11: Компонент1.D6_PWM, R6.Pin_1
  N12: Компонент1.D7, R8.Pin_1
  N13: R6.Pin_0, R7.Pin_0, R8.Pin_0
